// Logisim project ALU.circ as structural Verilog: 24 circuits, main circuit main
module main (
  input  S2,
  input  S1,
  input  S0,
  input  Enable,
  input  [7:0] A,
  input  [7:0] B,
  input  in_7,
  input  in_8,
  input  in_9,
  input  in_10,
  input  [7:0] in_11,
  input  [7:0] in_12,
  output [7:0] S,
  output [7:0] out_14,
  output out_15,
  output out_16
);

  ALU alu_1 (.S2(S2), .S1(S1), .S0(S0), .Enable(Enable), .A(A), .B(B), .S(S));
  ALUwithFlags aluwithflags_1 (
    .S2(in_7), .S1(in_8), .S0(in_9), .Enable(in_10), .A(in_11), .B(in_12), .S(out_14), .carry_flag(out_15),
    .borrow_flag(out_16));

  // Notes on the sheet:
  //   AND 000
  //   OR 001 
  //   XOR 010 
  //   XNOR 011 
  //   NOT 100 
  //   Suma 101 
  //   Resta 110 
  //   Multiplicación 111 
  //   Carry (suma) → me sobróo 1 bit
  //   Carry (resta) → no necesite pedir prestado
  //   Borrow → si tuve que pedir prestado
endmodule

module sum1bits (
  input  A,
  input  B,
  input  Cin,
  output S,
  output Cout
);

  wire nand_1_out, nand_2_out, nand_3_out, nand_4_out, nand_5_out, nand_6_out, nand_7_out, nand_8_out,
       nand_9_out, nand_10_out;

  nand nand_1 (nand_1_out, 1'b1, A);
  nand nand_2 (nand_2_out, 1'b1, B);
  nand nand_3 (nand_3_out, 1'b1, Cin);
  nand nand_4 (nand_4_out, nand_1_out, nand_2_out, Cin);
  nand nand_5 (nand_5_out, nand_1_out, B, nand_3_out);
  nand nand_6 (nand_6_out, A, nand_2_out, nand_3_out);
  nand nand_7 (nand_7_out, A, B, Cin);
  nand nand_8 (nand_8_out, B, Cin);
  nand nand_9 (nand_9_out, A, Cin);
  nand nand_10 (nand_10_out, A, B);
  nand nand_11 (S, nand_4_out, nand_5_out, nand_6_out, nand_7_out);
  nand nand_12 (Cout, nand_8_out, nand_9_out, nand_10_out);
endmodule

module sum2bits (
  input  B1,
  input  B0,
  input  A1,
  input  A0,
  input  Cout1,
  output Cout3,
  output S1,
  output S0
);

  wire sum1bits_1_cout;

  sum1bits sum1bits_1 (.A(A0), .B(B0), .Cin(Cout1), .S(S0), .Cout(sum1bits_1_cout));
  sum1bits sum1bits_2 (.A(A1), .B(B1), .Cin(sum1bits_1_cout), .S(S1), .Cout(Cout3));

  // Notes on the sheet:
  //   +
  //   [B1,B0] + [A1,A0]
endmodule

module sum4bits (
  input  B3,
  input  B2,
  input  B1,
  input  B0,
  input  A3,
  input  A2,
  input  A1,
  input  A0,
  input  Cout,
  output Carry,
  output S3,
  output S2,
  output S1,
  output S0
);

  wire sum2bits_1_cout3;

  sum2bits sum2bits_1 (.B1(B1), .B0(B0), .A1(A1), .A0(A0), .Cout1(Cout), .Cout3(sum2bits_1_cout3), .S1(S1), .S0(S0));
  sum2bits sum2bits_2 (.B1(B3), .B0(B2), .A1(A3), .A0(A2), .Cout1(sum2bits_1_cout3), .Cout3(Carry), .S1(S3), .S0(S2));

  // Notes on the sheet:
  //   +
  //   =
endmodule

module sum8bits (
  input  B7,
  input  B6,
  input  B5,
  input  B4,
  input  B3,
  input  B2,
  input  B1,
  input  B0,
  input  A7,
  input  A6,
  input  A5,
  input  A4,
  input  A3,
  input  A2,
  input  A1,
  input  A0,
  input  Cin,
  output Carry,
  output S7,
  output S6,
  output S5,
  output S4,
  output S3,
  output S2,
  output S1,
  output S0
);

  wire sum4bits_1_carry;

  sum4bits sum4bits_1 (
    .B3(B3), .B2(B2), .B1(B1), .B0(B0), .A3(A3), .A2(A2), .A1(A1), .A0(A0), .Cout(Cin),
    .Carry(sum4bits_1_carry), .S3(S3), .S2(S2), .S1(S1), .S0(S0));
  sum4bits sum4bits_2 (
    .B3(B7), .B2(B6), .B1(B5), .B0(B4), .A3(A7), .A2(A6), .A1(A5), .A0(A4), .Cout(sum4bits_1_carry),
    .Carry(Carry), .S3(S7), .S2(S6), .S1(S5), .S0(S4));

  // Notes on the sheet:
  //   +
  //   =
endmodule

module AND_op (
  input  [7:0] A,
  input  [7:0] B,
  output [7:0] S
);

  and and_1 (S[0], A[0], B[0]);
  and and_2 (S[1], A[1], B[1]);
  and and_3 (S[2], A[2], B[2]);
  and and_4 (S[3], A[3], B[3]);
  and and_5 (S[4], A[4], B[4]);
  and and_6 (S[5], A[5], B[5]);
  and and_7 (S[6], A[6], B[6]);
  and and_8 (S[7], A[7], B[7]);
endmodule

module OR_op (
  input  [7:0] A,
  input  [7:0] B,
  output [7:0] S
);

  or or_1 (S[0], A[0], B[0]);
  or or_2 (S[1], A[1], B[1]);
  or or_3 (S[2], A[2], B[2]);
  or or_4 (S[3], A[3], B[3]);
  or or_5 (S[4], A[4], B[4]);
  or or_6 (S[5], A[5], B[5]);
  or or_7 (S[6], A[6], B[6]);
  or or_8 (S[7], A[7], B[7]);
endmodule

module XOR_op (
  input  [7:0] A,
  input  [7:0] B,
  output [7:0] S
);

  xor xor_1 (S[0], A[0], B[0]);
  xor xor_2 (S[1], A[1], B[1]);
  xor xor_3 (S[2], A[2], B[2]);
  xor xor_4 (S[3], A[3], B[3]);
  xor xor_5 (S[4], A[4], B[4]);
  xor xor_6 (S[5], A[5], B[5]);
  xor xor_7 (S[6], A[6], B[6]);
  xor xor_8 (S[7], A[7], B[7]);
endmodule

module XNOR_op (
  input  [7:0] A,
  input  [7:0] B,
  output [7:0] S
);

  xnor xnor_1 (S[0], A[0], B[0]);
  xnor xnor_2 (S[1], A[1], B[1]);
  xnor xnor_3 (S[2], A[2], B[2]);
  xnor xnor_4 (S[3], A[3], B[3]);
  xnor xnor_5 (S[4], A[4], B[4]);
  xnor xnor_6 (S[5], A[5], B[5]);
  xnor xnor_7 (S[6], A[6], B[6]);
  xnor xnor_8 (S[7], A[7], B[7]);
endmodule

module SUM_op (
  input  [7:0] A,
  input  [7:0] B,
  input  cin,
  output carry,
  output [7:0] S
);

  sum8bits sum8bits_1 (
    .B7(B[7]), .B6(B[6]), .B5(B[5]), .B4(B[4]), .B3(B[3]), .B2(B[2]), .B1(B[1]), .B0(B[0]), .A7(A[7]),
    .A6(A[6]), .A5(A[5]), .A4(A[4]), .A3(A[3]), .A2(A[2]), .A1(A[1]), .A0(A[0]), .Cin(cin), .Carry(carry),
    .S7(S[7]), .S6(S[6]), .S5(S[5]), .S4(S[4]), .S3(S[3]), .S2(S[2]), .S1(S[1]), .S0(S[0]));
endmodule

module REST_op (
  input  [7:0] A,
  input  [7:0] B,
  output carry,
  output [7:0] S
);

  wire [7:0] not_op_1_s;

  NOT_op not_op_1 (.A(B), .S(not_op_1_s));
  SUM_op sum_op_1 (.A(not_op_1_s), .B(A), .cin(1'b1), .carry(carry), .S(S));

  // Notes on the sheet:
  //   -
endmodule

module NOT_op (
  input  [7:0] A,
  output [7:0] S
);

  not not_1 (S[0], A[0]);
  not not_2 (S[1], A[1]);
  not not_3 (S[2], A[2]);
  not not_4 (S[3], A[3]);
  not not_5 (S[4], A[4]);
  not not_6 (S[5], A[5]);
  not not_7 (S[6], A[6]);
  not not_8 (S[7], A[7]);
endmodule

module PRODUCT8bitsx1bit (
  input  [7:0] A,
  input  B,
  output [7:0] S
);

  AND_op and_op_1 (.A(A), .B({8{B}}), .S(S));
endmodule

module PRODUCT_op (
  input  [7:0] A,
  input  [7:0] B,
  output carry,
  output [7:0] S
);

  wire [7:0] displacement_1_m1, displacement_1_m2, displacement_1_m3, displacement_1_m4, displacement_1_m5,
       displacement_1_m6, displacement_1_m7, partial_products_1_s0, partial_products_1_s1,
       partial_products_1_s2, partial_products_1_s3, partial_products_1_s4, partial_products_1_s5,
       partial_products_1_s6, partial_products_1_s7;

  PARTIAL_PRODUCTS partial_products_1 (
    .A(A), .B0(B[0]), .B1(B[1]), .B2(B[2]), .B3(B[3]), .B4(B[4]), .B5(B[5]), .B6(B[6]), .B7(B[7]),
    .S0(partial_products_1_s0), .S1(partial_products_1_s1), .S2(partial_products_1_s2),
    .S3(partial_products_1_s3), .S4(partial_products_1_s4), .S5(partial_products_1_s5),
    .S6(partial_products_1_s6), .S7(partial_products_1_s7));
  DISPLACEMENT displacement_1 (
    .S1(partial_products_1_s1), .S2(partial_products_1_s2), .S3(partial_products_1_s3),
    .S4(partial_products_1_s4), .S5(partial_products_1_s5), .S6(partial_products_1_s6),
    .S7(partial_products_1_s7), .M1(displacement_1_m1), .M2(displacement_1_m2), .M3(displacement_1_m3),
    .M4(displacement_1_m4), .M5(displacement_1_m5), .M6(displacement_1_m6), .M7(displacement_1_m7));
  PARTIAL_SUM partial_sum_1 (
    .S0(partial_products_1_s0), .M1(displacement_1_m1), .M2(displacement_1_m2), .M3(displacement_1_m3),
    .M4(displacement_1_m4), .M5(displacement_1_m5), .M6(displacement_1_m6), .M7(displacement_1_m7),
    .carry(carry), .S(S));
endmodule

module MUX8x1 (
  input  S2,
  input  S1,
  input  S0,
  input  i7,
  input  i6,
  input  i5,
  input  i4,
  input  i3,
  input  i2,
  input  i1,
  input  i0,
  output Y
);

  wire and_1_out, and_2_out, and_3_out, and_4_out, and_5_out, and_6_out, and_7_out, and_8_out, not_1_out,
       not_2_out, not_3_out;

  not not_1 (not_1_out, S2);
  not not_2 (not_2_out, S1);
  not not_3 (not_3_out, S0);
  and and_1 (and_1_out, not_1_out, not_2_out, not_3_out, i0);
  and and_2 (and_2_out, not_1_out, not_2_out, S0, i1);
  and and_3 (and_3_out, not_1_out, S1, not_3_out, i2);
  and and_4 (and_4_out, not_1_out, S1, S0, i3);
  and and_5 (and_5_out, S2, not_2_out, not_3_out, i4);
  and and_6 (and_6_out, S2, not_2_out, S0, i5);
  and and_7 (and_7_out, S2, S1, not_3_out, i6);
  and and_8 (and_8_out, S2, S1, S0, i7);
  or or_1 (Y, and_1_out, and_2_out, and_3_out, and_4_out, and_5_out, and_6_out, and_7_out, and_8_out);
endmodule

module multi_8_1 (
  input  S2,
  input  S1,
  input  S0,
  input  [7:0] SUM_op,
  input  [7:0] REST_op,
  input  [7:0] PRODUCT_op,
  input  [7:0] NOT_op,
  input  [7:0] XNOR_op,
  input  [7:0] XOR_op,
  input  [7:0] OR_op,
  input  [7:0] AND_op,
  output OP0,
  output OP1,
  output OP2,
  output OP3,
  output OP4,
  output OP5,
  output OP6,
  output OP7
);

  MUX8x1 mux8x1_1 (
    .S2(S2), .S1(S1), .S0(S0), .i7(PRODUCT_op[0]), .i6(REST_op[0]), .i5(SUM_op[0]), .i4(NOT_op[0]),
    .i3(XNOR_op[0]), .i2(XOR_op[0]), .i1(OR_op[0]), .i0(AND_op[0]), .Y(OP0));
  MUX8x1 mux8x1_2 (
    .S2(S2), .S1(S1), .S0(S0), .i7(PRODUCT_op[4]), .i6(REST_op[4]), .i5(SUM_op[4]), .i4(NOT_op[4]),
    .i3(XNOR_op[4]), .i2(XOR_op[4]), .i1(OR_op[4]), .i0(AND_op[4]), .Y(OP4));
  MUX8x1 mux8x1_3 (
    .S2(S2), .S1(S1), .S0(S0), .i7(PRODUCT_op[1]), .i6(REST_op[1]), .i5(SUM_op[1]), .i4(NOT_op[1]),
    .i3(XNOR_op[1]), .i2(XOR_op[1]), .i1(OR_op[1]), .i0(AND_op[1]), .Y(OP1));
  MUX8x1 mux8x1_4 (
    .S2(S2), .S1(S1), .S0(S0), .i7(PRODUCT_op[5]), .i6(REST_op[5]), .i5(SUM_op[5]), .i4(NOT_op[5]),
    .i3(XNOR_op[5]), .i2(XOR_op[5]), .i1(OR_op[5]), .i0(AND_op[5]), .Y(OP5));
  MUX8x1 mux8x1_5 (
    .S2(S2), .S1(S1), .S0(S0), .i7(PRODUCT_op[2]), .i6(REST_op[2]), .i5(SUM_op[2]), .i4(NOT_op[2]),
    .i3(XNOR_op[2]), .i2(XOR_op[2]), .i1(OR_op[2]), .i0(AND_op[2]), .Y(OP2));
  MUX8x1 mux8x1_6 (
    .S2(S2), .S1(S1), .S0(S0), .i7(PRODUCT_op[6]), .i6(REST_op[6]), .i5(SUM_op[6]), .i4(NOT_op[6]),
    .i3(XNOR_op[6]), .i2(XOR_op[6]), .i1(OR_op[6]), .i0(AND_op[6]), .Y(OP6));
  MUX8x1 mux8x1_7 (
    .S2(S2), .S1(S1), .S0(S0), .i7(PRODUCT_op[3]), .i6(REST_op[3]), .i5(SUM_op[3]), .i4(NOT_op[3]),
    .i3(XNOR_op[3]), .i2(XOR_op[3]), .i1(OR_op[3]), .i0(AND_op[3]), .Y(OP3));
  MUX8x1 mux8x1_8 (
    .S2(S2), .S1(S1), .S0(S0), .i7(PRODUCT_op[7]), .i6(REST_op[7]), .i5(SUM_op[7]), .i4(NOT_op[7]),
    .i3(XNOR_op[7]), .i2(XOR_op[7]), .i1(OR_op[7]), .i0(AND_op[7]), .Y(OP7));
endmodule

module ALUwithFlags (
  input  S2,
  input  S1,
  input  S0,
  input  Enable,
  input  [7:0] A,
  input  [7:0] B,
  output [7:0] S,
  output carry_flag,
  output borrow_flag
);

  wire product_op_1_carry, rest_op_1_carry, sum_op_1_carry;
  wire [7:0] and_op_1_s, multi_8_1_1_op0, not_op_1_s, or_op_1_s, product_op_1_s, rest_op_1_s, sum_op_1_s,
       xnor_op_1_s, xor_op_1_s;

  AND_op and_op_1 (.A(A), .B(B), .S(and_op_1_s));
  OR_op or_op_1 (.A(A), .B(B), .S(or_op_1_s));
  NOT_op not_op_1 (.A(A), .S(not_op_1_s));
  XOR_op xor_op_1 (.A(A), .B(B), .S(xor_op_1_s));
  XNOR_op xnor_op_1 (.A(A), .B(B), .S(xnor_op_1_s));
  SUM_op sum_op_1 (.A(B), .B(A), .carry(sum_op_1_carry), .S(sum_op_1_s));  // open: cin
  REST_op rest_op_1 (.A(A), .B(B), .carry(rest_op_1_carry), .S(rest_op_1_s));
  // NoConnect on product_op_1_carry
  PRODUCT_op product_op_1 (.A(A), .B(B), .carry(product_op_1_carry), .S(product_op_1_s));
  multi_8_1 multi_8_1_1 (
    .S2(S2), .S1(S1), .S0(S0), .SUM_op(sum_op_1_s), .REST_op(rest_op_1_s), .PRODUCT_op(product_op_1_s),
    .NOT_op(not_op_1_s), .XNOR_op(xnor_op_1_s), .XOR_op(xor_op_1_s), .OR_op(or_op_1_s), .AND_op(and_op_1_s),
    .OP0(multi_8_1_1_op0[0]), .OP1(multi_8_1_1_op0[1]), .OP2(multi_8_1_1_op0[2]), .OP3(multi_8_1_1_op0[3]),
    .OP4(multi_8_1_1_op0[4]), .OP5(multi_8_1_1_op0[5]), .OP6(multi_8_1_1_op0[6]), .OP7(multi_8_1_1_op0[7]));
  flags flags_1 (
    .S2(S2), .S1(S1), .S0(S0), .carry(sum_op_1_carry), .not_borrow(rest_op_1_carry), .carry_flag(carry_flag),
    .borrow_flag(borrow_flag));
  AND_op and_op_2 (.A(multi_8_1_1_op0), .B({8{Enable}}), .S(S));
endmodule

module isSUM (
  input  S2,
  input  S1,
  input  S0,
  output F
);

  wire not_1_out;

  not not_1 (not_1_out, S1);
  and and_1 (F, S2, not_1_out, S0);
endmodule

module isREST (
  input  S2,
  input  S1,
  input  S0,
  output F
);

  wire not_1_out;

  not not_1 (not_1_out, S0);
  and and_1 (F, S2, S1, not_1_out);
endmodule

module flags (
  input  S2,
  input  S1,
  input  S0,
  input  carry,
  input  not_borrow,
  output carry_flag,
  output borrow_flag
);

  wire and_1_out, and_2_out, isrest_1_f, issum_1_f, not_1_out;

  isSUM issum_1 (.S2(S2), .S1(S1), .S0(S0), .F(issum_1_f));
  isREST isrest_1 (.S2(S2), .S1(S1), .S0(S0), .F(isrest_1_f));
  not not_1 (not_1_out, not_borrow);
  and and_1 (and_1_out, issum_1_f, carry);
  and and_2 (and_2_out, isrest_1_f, not_borrow);
  and and_3 (borrow_flag, isrest_1_f, not_1_out);
  or or_1 (carry_flag, and_1_out, and_2_out);
endmodule

module PARTIAL_PRODUCTS (
  input  [7:0] A,
  input  B0,
  input  B1,
  input  B2,
  input  B3,
  input  B4,
  input  B5,
  input  B6,
  input  B7,
  output [7:0] S0,
  output [7:0] S1,
  output [7:0] S2,
  output [7:0] S3,
  output [7:0] S4,
  output [7:0] S5,
  output [7:0] S6,
  output [7:0] S7
);

  PRODUCT8bitsx1bit product8bitsx1bit_1 (.A(A), .B(B0), .S(S0));
  PRODUCT8bitsx1bit product8bitsx1bit_2 (.A(A), .B(B1), .S(S1));
  PRODUCT8bitsx1bit product8bitsx1bit_3 (.A(A), .B(B2), .S(S2));
  PRODUCT8bitsx1bit product8bitsx1bit_4 (.A(A), .B(B3), .S(S3));
  PRODUCT8bitsx1bit product8bitsx1bit_5 (.A(A), .B(B4), .S(S4));
  PRODUCT8bitsx1bit product8bitsx1bit_6 (.A(A), .B(B5), .S(S5));
  PRODUCT8bitsx1bit product8bitsx1bit_7 (.A(A), .B(B6), .S(S6));
  PRODUCT8bitsx1bit product8bitsx1bit_8 (.A(A), .B(B7), .S(S7));
endmodule

module DISPLACEMENT (
  input  [7:0] S1,
  input  [7:0] S2,
  input  [7:0] S3,
  input  [7:0] S4,
  input  [7:0] S5,
  input  [7:0] S6,
  input  [7:0] S7,
  output [7:0] M1,
  output [7:0] M2,
  output [7:0] M3,
  output [7:0] M4,
  output [7:0] M5,
  output [7:0] M6,
  output [7:0] M7
);


  assign M1 = {S1[6:0], 1'b0};
  assign M2 = {S2[5:0], 2'b00};
  assign M3 = {S3[4:0], 3'b000};
  assign M4 = {S4[3:0], 4'b0000};
  assign M5 = {S5[2:0], {5{1'b0}}};
  assign M6 = {S6[1:0], {6{1'b0}}};
  assign M7 = {S7[0], {7{1'b0}}};
endmodule

module PARTIAL_SUM (
  input  [7:0] S0,
  input  [7:0] M1,
  input  [7:0] M2,
  input  [7:0] M3,
  input  [7:0] M4,
  input  [7:0] M5,
  input  [7:0] M6,
  input  [7:0] M7,
  output carry,
  output [7:0] S
);

  wire [7:0] sum_op_1_s, sum_op_2_s, sum_op_3_s, sum_op_4_s, sum_op_5_s, sum_op_6_s;

  SUM_op sum_op_1 (.A(S0), .B(M1), .cin(1'b0), .S(sum_op_1_s));  // open: carry
  SUM_op sum_op_2 (.A(sum_op_1_s), .B(M2), .S(sum_op_2_s));  // open: cin, carry
  SUM_op sum_op_3 (.A(sum_op_2_s), .B(M3), .S(sum_op_3_s));  // open: cin, carry
  SUM_op sum_op_4 (.A(sum_op_3_s), .B(M4), .S(sum_op_4_s));  // open: cin, carry
  SUM_op sum_op_5 (.A(sum_op_4_s), .B(M5), .S(sum_op_5_s));  // open: cin, carry
  SUM_op sum_op_6 (.A(sum_op_5_s), .B(M6), .S(sum_op_6_s));  // open: cin, carry
  SUM_op sum_op_7 (.A(sum_op_6_s), .B(M7), .carry(carry), .S(S));  // open: cin
endmodule

module ALU (
  input  S2,
  input  S1,
  input  S0,
  input  Enable,
  input  [7:0] A,
  input  [7:0] B,
  output [7:0] S
);

  wire product_op_1_carry, rest_op_1_carry, sum_op_1_carry;
  wire [7:0] and_op_1_s, multi_8_1_1_op0, not_op_1_s, or_op_1_s, product_op_1_s, rest_op_1_s, sum_op_1_s,
       xnor_op_1_s, xor_op_1_s;

  AND_op and_op_1 (.A(A), .B(B), .S(and_op_1_s));
  OR_op or_op_1 (.A(A), .B(B), .S(or_op_1_s));
  NOT_op not_op_1 (.A(A), .S(not_op_1_s));
  XOR_op xor_op_1 (.A(A), .B(B), .S(xor_op_1_s));
  XNOR_op xnor_op_1 (.A(A), .B(B), .S(xnor_op_1_s));
  // NoConnect on sum_op_1_carry
  SUM_op sum_op_1 (.A(B), .B(A), .carry(sum_op_1_carry), .S(sum_op_1_s));  // open: cin
  // NoConnect on rest_op_1_carry
  REST_op rest_op_1 (.A(A), .B(B), .carry(rest_op_1_carry), .S(rest_op_1_s));
  // NoConnect on product_op_1_carry
  PRODUCT_op product_op_1 (.A(A), .B(B), .carry(product_op_1_carry), .S(product_op_1_s));
  multi_8_1 multi_8_1_1 (
    .S2(S2), .S1(S1), .S0(S0), .SUM_op(sum_op_1_s), .REST_op(rest_op_1_s), .PRODUCT_op(product_op_1_s),
    .NOT_op(not_op_1_s), .XNOR_op(xnor_op_1_s), .XOR_op(xor_op_1_s), .OR_op(or_op_1_s), .AND_op(and_op_1_s),
    .OP0(multi_8_1_1_op0[0]), .OP1(multi_8_1_1_op0[1]), .OP2(multi_8_1_1_op0[2]), .OP3(multi_8_1_1_op0[3]),
    .OP4(multi_8_1_1_op0[4]), .OP5(multi_8_1_1_op0[5]), .OP6(multi_8_1_1_op0[6]), .OP7(multi_8_1_1_op0[7]));
  AND_op and_op_2 (.A(multi_8_1_1_op0), .B({8{Enable}}), .S(S));
endmodule
