// Logisim project sumNbits.circ as structural Verilog
module sum2bits (
  input  A,
  input  B,
  input  Cout1,
  output S,
  output Cout2
);

  wire nand_1_out, nand_2_out, nand_3_out, nand_4_out, nand_5_out, nand_6_out, nand_7_out, nand_8_out,
       nand_9_out, nand_10_out;

  nand nand_1 (nand_1_out, 1'b1, A);
  nand nand_2 (nand_2_out, 1'b1, B);
  nand nand_3 (nand_3_out, 1'b1, Cout1);
  nand nand_4 (nand_4_out, nand_1_out, nand_2_out, Cout1);
  nand nand_5 (nand_5_out, nand_1_out, B, nand_3_out);
  nand nand_6 (nand_6_out, A, nand_2_out, nand_3_out);
  nand nand_7 (nand_7_out, A, B, Cout1);
  nand nand_8 (nand_8_out, B, Cout1);
  nand nand_9 (nand_9_out, A, Cout1);
  nand nand_10 (nand_10_out, A, B);
  nand nand_11 (S, nand_4_out, nand_5_out, nand_6_out, nand_7_out);
  nand nand_12 (Cout2, nand_8_out, nand_9_out, nand_10_out);
endmodule

module sum4bits (
  input  B1,
  input  B0,
  input  A1,
  input  A0,
  input  Cout1,
  output Cout3,
  output S1,
  output S0
);

  wire sum2bits_1_cout2;

  sum2bits sum2bits_1 (.A(A0), .B(B0), .Cout1(Cout1), .S(S0), .Cout2(sum2bits_1_cout2));
  sum2bits sum2bits_2 (.A(A1), .B(B1), .Cout1(sum2bits_1_cout2), .S(S1), .Cout2(Cout3));

  // Notes on the sheet:
  //   +
  //   [B1,B0] + [A1,A0]
endmodule

module sum8bits (
  input  B3,
  input  B2,
  input  B1,
  input  B0,
  input  A3,
  input  A2,
  input  A1,
  input  A0,
  input  Cout,
  output Carry,
  output S3,
  output S2,
  output S1,
  output S0
);

  wire sum4bits_1_cout3;

  sum4bits sum4bits_1 (.B1(B1), .B0(B0), .A1(A1), .A0(A0), .Cout1(Cout), .Cout3(sum4bits_1_cout3), .S1(S1), .S0(S0));
  sum4bits sum4bits_2 (.B1(B3), .B0(B2), .A1(A3), .A0(A2), .Cout1(sum4bits_1_cout3), .Cout3(Carry), .S1(S3), .S0(S2));

  // Notes on the sheet:
  //   +
  //   =
endmodule

module sum16bits (
  input  B7,
  input  B6,
  input  B5,
  input  B4,
  input  B3,
  input  B2,
  input  B1,
  input  B0,
  input  A7,
  input  A6,
  input  A5,
  input  A4,
  input  A3,
  input  A2,
  input  A1,
  input  A0,
  input  Cout,
  output Carry,
  output S7,
  output S6,
  output S5,
  output S4,
  output S3,
  output S2,
  output S1,
  output S0
);

  wire sum8bits_1_carry;

  sum8bits sum8bits_1 (
    .B3(B3), .B2(B2), .B1(B1), .B0(B0), .A3(A3), .A2(A2), .A1(A1), .A0(A0), .Cout(Cout),
    .Carry(sum8bits_1_carry), .S3(S3), .S2(S2), .S1(S1), .S0(S0));
  sum8bits sum8bits_2 (
    .B3(B7), .B2(B6), .B1(B5), .B0(B4), .A3(A7), .A2(A6), .A1(A5), .A0(A4), .Cout(sum8bits_1_carry),
    .Carry(Carry), .S3(S7), .S2(S6), .S1(S5), .S0(S4));

  // Notes on the sheet:
  //   +
  //   =
endmodule
